# Fritzing sketch data_collection_uno_mode (saved by Fritzing 0.9.3b)
breadboards: 1

parts:
  Composant1 = Arduino Uno (Rev3)
  R1 = Resistor [tolerance=±5% resistance=10k package=THT]
  S1 = Pushbutton [package="[THT]"]
  LED1 = LED - 5mm [color="Red (633nm)" package="5 mm [THT]"]
  LED2 = LED - 5mm [color="White (4500K)" package="5 mm [THT]"]
  LED3 = LED - 5mm [color="Green (570nm)" package="5 mm [THT]"]  # not connected
  R2 = Resistor [tolerance=±5% resistance=320 package="1206 [SMD]"]

nets:
  N1: Composant1.GND, R1.Pin_0, R2.Pin_0
  N2: Composant1.D3_PWM, R1.Pin_1, S1.Pin_3, S1.Pin_4
  N3: Composant1.D5_PWM, LED1.cathode
  N4: Composant1.D6_PWM, LED2.cathode
  N5: Composant1.5V, S1.Pin_1, S1.Pin_2
  N6: LED1.anode, LED2.anode, R2.Pin_1
